// Logisim project Booth.circ as structural Verilog: 2 circuits, main circuit Bit4_Sync_Counter
module Bit4_Sync_Counter (
  input  CLK,
  input  CLR,
  output [3:0] Out
);

  wire and_1_out, and_2_out;

  T_Flip_Flop t_ff_1 (.T(and_1_out), .clk(CLK), .Q(Out[3]), .reset(CLR));  // open: Qn, preset
  and and_1 (and_1_out, Out[2], and_2_out);
  T_Flip_Flop t_ff_2 (.T(and_2_out), .clk(CLK), .Q(Out[2]), .reset(CLR));  // open: Qn, preset
  and and_2 (and_2_out, Out[1], Out[0]);
  T_Flip_Flop t_ff_3 (.T(Out[0]), .clk(CLK), .Q(Out[1]), .reset(CLR));  // open: Qn, preset
  T_Flip_Flop t_ff_4 (.T(1'b1), .clk(CLK), .Q(Out[0]), .reset(CLR));  // open: Qn, preset
endmodule

module Sequence_Counter (
  input  CLK_IN,
  input  [3:0] START,
  input  SET,
  input  CLR,
  output [3:0] Out,
  output CLK_OUT
);

  wire and_2_out, and_3_out, or_1_out, t_ff_2_qn, t_ff_3_qn, t_ff_4_qn;
  wire [3:0] controlled_buffer_1_out;

  or or_1 (or_1_out, Out[0], Out[1], Out[2], Out[3]);
  and and_1 (CLK_OUT, CLK_IN, or_1_out);
  assign controlled_buffer_1_out = SET ? START : 4'bz;  // Controlled_Buffer controlled_buffer_1
  T_Flip_Flop t_ff_1 (
    .T(and_2_out), .clk(CLK_OUT), .Q(Out[3]), .reset(CLR), .preset(controlled_buffer_1_out[3]));  // open: Qn
  and and_2 (and_2_out, t_ff_2_qn, and_3_out);
  T_Flip_Flop t_ff_2 (
    .T(and_3_out), .clk(CLK_OUT), .Q(Out[2]), .Qn(t_ff_2_qn), .reset(CLR), .preset(controlled_buffer_1_out[2]));
  and and_3 (and_3_out, t_ff_3_qn, t_ff_4_qn);
  T_Flip_Flop t_ff_3 (
    .T(t_ff_4_qn), .clk(CLK_OUT), .Q(Out[1]), .Qn(t_ff_3_qn), .reset(CLR), .preset(controlled_buffer_1_out[1]));
  T_Flip_Flop t_ff_4 (
    .T(1'b1), .clk(CLK_OUT), .Q(Out[0]), .Qn(t_ff_4_qn), .reset(CLR), .preset(controlled_buffer_1_out[0]));
endmodule
