// Logisim project CIRCUITS.circ as structural Verilog: 26 circuits, main circuit HalfAdder
// HA
module HalfAdder (
  input  A,
  input  B,
  output Sum,
  output Carry_Out
);

  and and_1 (Carry_Out, A, B);
  xor xor_1 (Sum, A, B);
endmodule

// FA
module FullAdder (
  input  Carry_In,
  input  A,
  input  B,
  output Sum,
  output Carry_Out
);

  wire halfadder_1_carry_out, halfadder_1_sum, halfadder_2_carry_out;

  HalfAdder halfadder_1 (.A(A), .B(B), .Sum(halfadder_1_sum), .Carry_Out(halfadder_1_carry_out));
  HalfAdder halfadder_2 (.A(halfadder_1_sum), .B(Carry_In), .Sum(Sum), .Carry_Out(halfadder_2_carry_out));
  or or_1 (Carry_Out, halfadder_2_carry_out, halfadder_1_carry_out);
endmodule

module SRLatch (
  input  S,
  input  CLK,
  input  R,
  output Q,
  output Qn
);

  wire nand_1_out, nand_2_out;

  nand nand_1 (nand_1_out, S, CLK);
  nand nand_2 (nand_2_out, CLK, R);
  nand nand_3 (Q, nand_1_out, Qn);
  nand nand_4 (Qn, Q, nand_2_out);
endmodule

module Mem_4Bit (
  input  CLK,
  input  [3:0] Data_In,
  input  SET,
  input  RESET,
  input  Enable,
  output [3:0] Data_Out
);

  D_FF d_ff_1 (.Din(Data_In[0]), .CLK(CLK), .Dout(Data_Out[0]), .Enable(Enable), .SET(SET), .RESET(RESET));
  D_FF d_ff_2 (.Din(Data_In[1]), .CLK(CLK), .Dout(Data_Out[1]), .Enable(Enable), .SET(SET), .RESET(RESET));
  D_FF d_ff_3 (.Din(Data_In[2]), .CLK(CLK), .Dout(Data_Out[2]), .Enable(Enable), .SET(SET), .RESET(RESET));
  D_FF d_ff_4 (.Din(Data_In[3]), .CLK(CLK), .Dout(Data_Out[3]), .Enable(Enable), .SET(SET), .RESET(RESET));
endmodule

module Adder_4Bit (
  input  [3:0] B,
  input  [3:0] A,
  output [3:0] Result,
  output Overflow
);

  wire fulladder_2_carry_out, fulladder_3_carry_out, fulladder_4_carry_out;

  FullAdder fulladder_1 (.Carry_In(fulladder_2_carry_out), .A(A[3]), .B(B[3]), .Sum(Result[3]), .Carry_Out(Overflow));
  FullAdder fulladder_2 (
    .Carry_In(fulladder_3_carry_out), .A(A[2]), .B(B[2]), .Sum(Result[2]), .Carry_Out(fulladder_2_carry_out));
  FullAdder fulladder_3 (
    .Carry_In(fulladder_4_carry_out), .A(A[1]), .B(B[1]), .Sum(Result[1]), .Carry_Out(fulladder_3_carry_out));
  FullAdder fulladder_4 (.Carry_In(1'b0), .A(A[0]), .B(B[0]), .Sum(Result[0]), .Carry_Out(fulladder_4_carry_out));
endmodule

// D
module D_FF (
  input  SET,
  input  Din,
  input  CLK,
  input  Enable,
  input  RESET,
  output Dout
);

  wire and_1_out, and_2_out, nand_1_out, nand_2_out, nand_4_out, not_1_out, not_2_out, not_3_out, not_4_out,
       not_5_out, not_6_out;

  not not_1 (not_1_out, not_2_out);
  not not_2 (not_2_out, CLK);
  not not_3 (not_3_out, not_1_out);
  and and_1 (and_1_out, not_3_out, CLK);
  and and_2 (and_2_out, and_1_out, Enable);
  not not_4 (not_4_out, Din);
  nand nand_1 (nand_1_out, Din, and_2_out);
  nand nand_2 (nand_2_out, and_2_out, not_4_out);
  not not_5 (not_5_out, SET);
  not not_6 (not_6_out, RESET);
  nand nand_3 (Dout, nand_1_out, not_5_out, nand_4_out);
  nand nand_4 (nand_4_out, Dout, not_6_out, nand_2_out);
endmodule

// Grid_5X9
module Display (
  input  B,
  input  A,
  input  C,
  input  G,
  input  F,
  input  D,
  input  E,
  output [8:0] D4,
  output [8:0] D3,
  output [8:0] D2,
  output [8:0] D0,
  output [8:0] D1
);


  assign D0 = {1'b0, {3{D}}, 1'b0, {3{C}}, 1'b0};
  assign D1 = {B, 3'b000, G, 3'b000, E};
  assign D2 = {B, 3'b000, G, 3'b000, E};
  assign D3 = {B, 3'b000, G, 3'b000, E};
  assign D4 = {1'b0, {3{F}}, 1'b0, {3{A}}, 1'b0};
endmodule

module Display_5PANEL (
  input  ENABLE,
  input  RESET,
  input  SET,
  input  LOAD_SHIFT,
  input  [7:0] in_5,
  input  SERIAL_IN,
  input  ENABLE_CLK
);

  wire and_1_out, CLK_out, or_1_out;
  wire [7:0] mem_8bit_1_dout, mem_8bit_2_dout, mem_8bit_3_dout, mem_8bit_4_dout, mem_8bit_5_dout,
       multiplexer_1_out;
  wire [8:0] display_1_d0, display_1_d1, display_1_d2, display_1_d3, display_1_d4, display_2_d0,
       display_2_d1, display_2_d2, display_2_d3, display_2_d4, display_3_d0, display_3_d1, display_3_d2,
       display_3_d3, display_3_d4, display_4_d0, display_4_d1, display_4_d2, display_4_d3, display_4_d4,
       display_5_d0, display_5_d1, display_5_d2, display_5_d3, display_5_d4;

  DotMatrix #(.matrixrows(9)) dotmatrix_1 (
    .col0(display_1_d0), .col1(display_1_d1), .col2(display_1_d3), .col3(display_1_d2), .col4(display_1_d4));
  Display display_1 (
    .A(mem_8bit_1_dout[6]), .B(mem_8bit_1_dout[5]), .F(mem_8bit_1_dout[1]), .G(mem_8bit_1_dout[0]),
    .D(mem_8bit_1_dout[3]), .E(mem_8bit_1_dout[2]), .C(mem_8bit_1_dout[4]), .D4(display_1_d4),
    .D3(display_1_d3), .D1(display_1_d1), .D0(display_1_d0), .D2(display_1_d2));
  Mem_8Bit mem_8bit_1 (
    .Enable(ENABLE), .Din(multiplexer_1_out), .Dout(mem_8bit_1_dout), .CLK(or_1_out), .SET(RESET), .RESET(SET));
  Multiplexer #(.width(8), .enable("false")) multiplexer_1 (
    .in0(in_5), .in1(mem_8bit_5_dout), .out(multiplexer_1_out), .sel(LOAD_SHIFT));
  DotMatrix #(.matrixrows(9)) dotmatrix_2 (
    .col0(display_2_d0), .col1(display_2_d1), .col2(display_2_d3), .col3(display_2_d2), .col4(display_2_d4));
  Display display_2 (
    .A(mem_8bit_2_dout[6]), .B(mem_8bit_2_dout[5]), .F(mem_8bit_2_dout[1]), .G(mem_8bit_2_dout[0]),
    .D(mem_8bit_2_dout[3]), .E(mem_8bit_2_dout[2]), .C(mem_8bit_2_dout[4]), .D4(display_2_d4),
    .D3(display_2_d3), .D1(display_2_d1), .D0(display_2_d0), .D2(display_2_d2));
  Mem_8Bit mem_8bit_2 (
    .Enable(ENABLE), .Din(mem_8bit_1_dout), .Dout(mem_8bit_2_dout), .CLK(or_1_out), .SET(RESET), .RESET(SET));
  DotMatrix #(.matrixrows(9)) dotmatrix_3 (
    .col0(display_3_d0), .col1(display_3_d1), .col2(display_3_d3), .col3(display_3_d2), .col4(display_3_d4));
  DotMatrix #(.matrixrows(9)) dotmatrix_4 (
    .col0(display_4_d0), .col1(display_4_d1), .col2(display_4_d3), .col3(display_4_d2), .col4(display_4_d4));
  Display display_3 (
    .A(mem_8bit_3_dout[6]), .B(mem_8bit_3_dout[5]), .F(mem_8bit_3_dout[1]), .G(mem_8bit_3_dout[0]),
    .D(mem_8bit_3_dout[3]), .E(mem_8bit_3_dout[2]), .C(mem_8bit_3_dout[4]), .D4(display_3_d4),
    .D3(display_3_d3), .D1(display_3_d1), .D0(display_3_d0), .D2(display_3_d2));
  Mem_8Bit mem_8bit_3 (
    .Enable(ENABLE), .Din(mem_8bit_2_dout), .Dout(mem_8bit_3_dout), .CLK(or_1_out), .SET(RESET), .RESET(SET));
  Display display_4 (
    .A(mem_8bit_4_dout[6]), .B(mem_8bit_4_dout[5]), .F(mem_8bit_4_dout[1]), .G(mem_8bit_4_dout[0]),
    .D(mem_8bit_4_dout[3]), .E(mem_8bit_4_dout[2]), .C(mem_8bit_4_dout[4]), .D4(display_4_d4),
    .D3(display_4_d3), .D1(display_4_d1), .D0(display_4_d0), .D2(display_4_d2));
  Mem_8Bit mem_8bit_4 (
    .Enable(ENABLE), .Din(mem_8bit_3_dout), .Dout(mem_8bit_4_dout), .CLK(or_1_out), .SET(RESET), .RESET(SET));
  DotMatrix #(.matrixrows(9)) dotmatrix_5 (
    .col0(display_5_d0), .col1(display_5_d1), .col2(display_5_d3), .col3(display_5_d2), .col4(display_5_d4));
  Display display_5 (
    .A(mem_8bit_5_dout[6]), .B(mem_8bit_5_dout[5]), .F(mem_8bit_5_dout[1]), .G(mem_8bit_5_dout[0]),
    .D(mem_8bit_5_dout[3]), .E(mem_8bit_5_dout[2]), .C(mem_8bit_5_dout[4]), .D4(display_5_d4),
    .D3(display_5_d3), .D1(display_5_d1), .D0(display_5_d0), .D2(display_5_d2));
  Mem_8Bit mem_8bit_5 (
    .Enable(ENABLE), .Din(mem_8bit_4_dout), .Dout(mem_8bit_5_dout), .CLK(or_1_out), .SET(RESET), .RESET(SET));
  and and_1 (and_1_out, CLK_out, ENABLE_CLK);
  or or_1 (or_1_out, and_1_out, SERIAL_IN);
  Clock CLK (.out(CLK_out));
endmodule

// Bit8
module Mem_8Bit (
  input  [7:0] Din,
  input  CLK,
  input  SET,
  input  RESET,
  input  Enable,
  output [7:0] Dout
);

  Mem_4Bit mem_4bit_1 (.CLK(CLK), .SET(RESET), .Enable(Enable), .Data_In(Din[3:0]), .RESET(SET), .Data_Out(Dout[3:0]));
  Mem_4Bit mem_4bit_2 (.CLK(CLK), .SET(RESET), .Enable(Enable), .Data_In(Din[7:4]), .RESET(SET), .Data_Out(Dout[7:4]));
endmodule

module Circular_Shift (
  input  [7:0] in_1,
  input  in_2,
  output [7:0] out_3,
  output [7:0] out_4,
  output [7:0] out_5,
  output [7:0] out_6
);

  wire mem_8bit_1_p4;

  // Mem_8Bit mem_8bit_1: pin names not known; wires that end beside it: out_3, in_1, in_2, mem_8bit_1_p4
  Clock clock_1 (.out(mem_8bit_1_p4));
  // Mem_8Bit mem_8bit_2: pin names not known; wires that end beside it: out_4, out_3, in_2, mem_8bit_1_p4
  // Mem_8Bit mem_8bit_3: pin names not known; wires that end beside it: out_5, out_4, in_2, mem_8bit_1_p4
  // Mem_8Bit mem_8bit_4: pin names not known; wires that end beside it: out_6, out_5, in_2, mem_8bit_1_p4
endmodule

module JK_FF (
  input  Set,
  input  J,
  input  CLK,
  input  K,
  input  Reset,
  output Q,
  output Qn
);

  wire and_1_out, and_2_out, and_3_out, nand_1_out, nand_2_out, not_1_out, not_2_out, not_3_out, or_1_out,
       or_2_out;

  and and_1 (and_1_out, Qn, J);
  and and_2 (and_2_out, K, Q);
  not not_1 (not_1_out, CLK);
  not not_2 (not_2_out, not_3_out);
  not not_3 (not_3_out, not_1_out);
  or or_1 (or_1_out, Set, and_1_out);
  and and_3 (and_3_out, not_2_out, CLK);
  or or_2 (or_2_out, and_2_out, Reset);
  nand nand_1 (nand_1_out, or_1_out, and_3_out);
  nand nand_2 (nand_2_out, and_3_out, or_2_out);
  nand nand_3 (Q, nand_1_out, Qn);
  nand nand_4 (Qn, Q, nand_2_out);
endmodule

module MUX_2X1 (
  input  D0,
  input  D1,
  input  S0,
  output Y
);

  wire and_1_out, and_2_out, not_1_out;

  not not_1 (not_1_out, S0);
  and and_1 (and_1_out, D0, not_1_out);
  or or_1 (Y, and_1_out, and_2_out);
  and and_2 (and_2_out, D1, S0);
endmodule

module D_From_JK_FF (
  input  Din,
  input  CLK,
  input  Clear,
  output Dout
);

  wire and_1_out, and_2_out, and_3_out, nand_1_out, nand_2_out, nand_4_out, not_1_out, not_2_out, not_3_out,
       not_4_out, or_1_out;

  not not_1 (not_1_out, Din);
  and and_1 (and_1_out, nand_4_out, Din);
  not not_2 (not_2_out, CLK);
  not not_3 (not_3_out, not_2_out);
  and and_2 (and_2_out, not_1_out, Dout);
  not not_4 (not_4_out, not_3_out);
  and and_3 (and_3_out, not_4_out, CLK);
  or or_1 (or_1_out, and_2_out, Clear);
  nand nand_1 (nand_1_out, and_1_out, and_3_out);
  nand nand_2 (nand_2_out, and_3_out, or_1_out);
  nand nand_3 (Dout, nand_1_out, nand_4_out);
  nand nand_4 (nand_4_out, Dout, nand_2_out);
endmodule

module Booth (
  input  [3:0] Multiplicand,
  input  [3:0] Multiplier,
  input  in_3,
  input  RESET,
  input  [3:0] SCin,
  input  Set_SC,
  input  in_7,
  input  Enable,
  input  Shift,
  input  Shift_2,
  input  ASHR,
  input  ASHR_2,
  input  in_13,
  output [3:0] Sequence_Counter,
  output Q_7f0a6f3e,
  output [3:0] Accumulator,
  output [3:0] Q,
  output [3:0] M_Comp,
  output [3:0] M,
  output [3:0] out_20,
  output [3:0] out_21,
  output [3:0] out_22
);

  wire Accumulator_lsb, and_1_out, CLK_out, Multiplier_lsb, not_1_out, not_2_out, not_3_out, or_1_out,
       sequence_counter_1_clk_out, xor_1_out;
  wire [3:0] not_4_out;

  Clock CLK (.out(CLK_out));
  Sequence_counter sequence_counter_1 (
    .Out(Sequence_Counter), .CLK_IN(CLK_out), .CLK_OUT(sequence_counter_1_clk_out), .SeqStart(SCin),
    .CLR(RESET), .Load_SET(Set_SC));
  not not_1 (not_1_out, or_1_out);
  or or_1 (or_1_out, sequence_counter_1_clk_out, in_13);
  not not_2 (not_2_out, not_1_out);
  and and_1 (and_1_out, not_2_out, xor_1_out);
  Adder_4Bit Full_Adder (.B(out_22), .A(out_20), .Result(out_21));  // open: Overflow
  Bit4_RShift_Reg u_Accumulator (
    .MSB(in_7), .ASHR_Mode(ASHR), .LSB(Accumulator_lsb), .CLK(not_1_out), .Enable(Enable),
    .Output(Accumulator), .Shift(Shift), .Load_E(and_1_out), .Load_In(out_21));
  Mem_4Bit mem_4bit_1 (
    .CLK(not_3_out), .Enable(Enable), .Data_In(Accumulator), .RESET(RESET), .Data_Out(out_20));  // open: SET
  Bit4_RShift_Reg u_Multiplier (
    .MSB(Accumulator_lsb), .ASHR_Mode(ASHR_2), .LSB(Multiplier_lsb), .CLK(not_1_out), .Enable(Enable),
    .Output(Q), .Shift(Shift_2), .Load_E(in_3), .Load_In(Multiplier));
  not not_3 (not_3_out, not_1_out);
  xor xor_1 (xor_1_out, Q[0], Q_7f0a6f3e);
  MUX_4X1 MUX_4X1 (.D1(Multiplicand), .D2(M_Comp), .S1(Q[0]), .S0(Q_7f0a6f3e), .Y(out_22));  // open: D0, D3
  D_FF d_ff_1 (.Din(Multiplier_lsb), .CLK(not_1_out), .Dout(Q_7f0a6f3e), .Enable(Enable), .RESET(RESET));  // open: SET
  Adder_4Bit Full_Adder_2 (.B(not_4_out), .A(4'b0001), .Result(M_Comp));  // open: Overflow
  assign not_4_out = ~Multiplicand;  // NOT_Gate not_4, 4 bits wide

  assign M = Multiplicand;

  // Other names for the same wires on the sheet: Accum_In[3:0] = out_21
endmodule

module Bit4_Sync_Counter (
  input  CLK,
  input  CLR,
  output [3:0] Out
);

  wire and_1_out, and_2_out;

  T_Flip_Flop t_ff_1 (.T(and_1_out), .clk(CLK), .Q(Out[3]), .reset(CLR));  // open: Qn, preset
  and and_1 (and_1_out, Out[2], and_2_out);
  T_Flip_Flop t_ff_2 (.T(and_2_out), .clk(CLK), .Q(Out[2]), .reset(CLR));  // open: Qn, preset
  and and_2 (and_2_out, Out[1], Out[0]);
  T_Flip_Flop t_ff_3 (.T(Out[0]), .clk(CLK), .Q(Out[1]), .reset(CLR));  // open: Qn, preset
  T_Flip_Flop t_ff_4 (.T(1'b1), .clk(CLK), .Q(Out[0]), .reset(CLR));  // open: Qn, preset
endmodule

// SC
module Sequence_counter (
  input  CLK_IN,
  input  [3:0] SeqStart,
  input  Load_SET,
  input  CLR,
  output [3:0] Out,
  output CLK_OUT
);

  wire and_2_out, and_3_out, or_1_out, t_ff_2_qn, t_ff_3_qn, t_ff_4_qn;
  wire [3:0] controlled_buffer_1_out;

  or or_1 (or_1_out, Out[0], Out[1], Out[2], Out[3]);
  and and_1 (CLK_OUT, CLK_IN, or_1_out);
  assign controlled_buffer_1_out = Load_SET ? SeqStart : 4'bz;  // Controlled_Buffer controlled_buffer_1
  T_Flip_Flop t_ff_1 (
    .T(and_2_out), .clk(CLK_OUT), .Q(Out[3]), .reset(CLR), .preset(controlled_buffer_1_out[3]));  // open: Qn
  and and_2 (and_2_out, t_ff_2_qn, and_3_out);
  T_Flip_Flop t_ff_2 (
    .T(and_3_out), .clk(CLK_OUT), .Q(Out[2]), .Qn(t_ff_2_qn), .reset(CLR), .preset(controlled_buffer_1_out[2]));
  and and_3 (and_3_out, t_ff_3_qn, t_ff_4_qn);
  T_Flip_Flop t_ff_3 (
    .T(t_ff_4_qn), .clk(CLK_OUT), .Q(Out[1]), .Qn(t_ff_3_qn), .reset(CLR), .preset(controlled_buffer_1_out[1]));
  T_Flip_Flop t_ff_4 (
    .T(1'b1), .clk(CLK_OUT), .Q(Out[0]), .Qn(t_ff_4_qn), .reset(CLR), .preset(controlled_buffer_1_out[0]));
endmodule

// ShiftReg_4BIT
module Bit4_RShift_Reg (
  input  Shift,
  input  MSB,
  input  ASHR_Mode,
  input  CLK,
  input  Enable,
  input  [3:0] Load_In,
  input  Load_E,
  output LSB,
  output [3:0] Output
);

  wire and_1_out, and_2_out, and_3_out, and_4_out, and_5_out, and_6_out, and_7_out, and_8_out, and_9_out,
       and_10_out, and_11_out, and_12_out, mux_2x1_1_y, not_1_out, not_2_out, not_3_out, not_4_out;

  MUX_2X1 mux_2x1_1 (.D0(MSB), .D1(Output[3]), .S0(ASHR_Mode), .Y(mux_2x1_1_y));
  and and_1 (and_1_out, Shift, mux_2x1_1_y);
  and and_2 (and_2_out, Load_E, not_1_out);
  not not_1 (not_1_out, Load_In[3]);
  and and_3 (and_3_out, Shift, Output[3]);
  D_FF d_ff_1 (.Din(and_1_out), .CLK(CLK), .Dout(Output[3]), .Enable(Enable), .SET(and_4_out), .RESET(and_2_out));
  and and_4 (and_4_out, Load_In[3], Load_E);
  not not_2 (not_2_out, Load_In[2]);
  and and_5 (and_5_out, Load_E, not_2_out);
  D_FF d_ff_2 (.Din(and_3_out), .CLK(CLK), .Dout(Output[2]), .Enable(Enable), .SET(and_7_out), .RESET(and_5_out));
  and and_6 (and_6_out, Shift, Output[2]);
  and and_7 (and_7_out, Load_In[2], Load_E);
  not not_3 (not_3_out, Load_In[1]);
  and and_8 (and_8_out, Load_E, not_3_out);
  D_FF d_ff_3 (.Din(and_6_out), .CLK(CLK), .Dout(Output[1]), .Enable(Enable), .SET(and_9_out), .RESET(and_8_out));
  and and_9 (and_9_out, Load_In[1], Load_E);
  and and_10 (and_10_out, Shift, Output[1]);
  and and_11 (and_11_out, Load_E, not_4_out);
  not not_4 (not_4_out, Load_In[0]);
  D_FF d_ff_4 (.Din(and_10_out), .CLK(CLK), .Dout(LSB), .Enable(Enable), .SET(and_12_out), .RESET(and_11_out));
  and and_12 (and_12_out, Load_In[0], Load_E);

  assign Output[0] = LSB;
endmodule

module MUX_4X1 (
  input  [3:0] D0,
  input  [3:0] D1,
  input  [3:0] D2,
  input  [3:0] D3,
  input  S1,
  input  S0,
  output [3:0] Y
);

  wire [3:0] and_1_out, and_2_out, and_3_out, and_4_out, not_1_out, not_2_out, pull_resistor_1_node,
       pull_resistor_2_node;

  Pull_Resistor pull_resistor_1 (.node(pull_resistor_1_node));
  assign not_1_out = ~pull_resistor_2_node;  // NOT_Gate not_1, 4 bits wide
  assign not_2_out = ~pull_resistor_1_node;  // NOT_Gate not_2, 4 bits wide
  Pull_Resistor pull_resistor_2 (.node(pull_resistor_2_node));
  assign pull_resistor_2_node = S0 ? 4'b1111 : 4'bz;  // Controlled_Buffer controlled_buffer_1
  assign pull_resistor_1_node = S1 ? 4'b1111 : 4'bz;  // Controlled_Buffer controlled_buffer_2
  assign and_1_out = D0 & not_2_out & not_1_out;  // AND_Gate and_1, 4 bits wide
  assign and_2_out = D1 & not_2_out & pull_resistor_2_node;  // AND_Gate and_2, 4 bits wide
  assign and_3_out = D2 & pull_resistor_1_node & not_1_out;  // AND_Gate and_3, 4 bits wide
  assign and_4_out = D3 & pull_resistor_2_node & pull_resistor_1_node;  // AND_Gate and_4, 4 bits wide
  assign Y = and_1_out | and_2_out | and_3_out | and_4_out;  // OR_Gate or_1, 4 bits wide
endmodule

module DeMux_1x4 (
  input  Din,
  input  S1,
  input  S0,
  output [3:0] Y
);

  wire not_1_out, not_2_out;

  not not_1 (not_1_out, S1);
  not not_2 (not_2_out, S0);
  and and_1 (Y[0], Din, not_1_out, not_2_out);
  and and_2 (Y[1], Din, not_1_out, S0);
  and and_3 (Y[2], Din, S1, not_2_out);
  and and_4 (Y[3], Din, S1, S0);
endmodule

module Decoder_2_4 (
  input  S0,
  input  S1,
  input  E,
  output D0,
  output D1,
  output D2,
  output D3
);

  wire not_1_out, not_2_out;

  not not_1 (not_1_out, S1);
  not not_2 (not_2_out, S0);
  and and_1 (D0, not_2_out, not_1_out, E);
  and and_2 (D1, S0, not_1_out, E);
  and and_3 (D2, not_2_out, S1, E);
  and and_4 (D3, S0, S1, E);
endmodule

module Decoder_4_16 (
  input  S3,
  input  S2,
  input  S1,
  input  S0,
  input  E,
  output D0,
  output D1,
  output D2,
  output D3,
  output D4,
  output D5,
  output D6,
  output D7,
  output D8,
  output D9,
  output D10,
  output D11,
  output D12,
  output D13,
  output D14,
  output D15
);

  wire and_1_out, and_2_out, and_3_out, and_4_out, not_1_out, not_2_out;

  not not_1 (not_1_out, S2);
  not not_2 (not_2_out, S3);
  and and_1 (and_1_out, not_2_out, E, not_1_out);
  and and_2 (and_2_out, S2, E, not_2_out);
  and and_3 (and_3_out, not_1_out, E, S3);
  and and_4 (and_4_out, S2, E, S3);
  Decoder_2_4 decoder_2_4_1 (.S0(S0), .S1(S1), .E(and_1_out), .D0(D0), .D1(D1), .D2(D2), .D3(D3));
  Decoder_2_4 decoder_2_4_2 (.S0(S0), .S1(S1), .E(and_2_out), .D0(D4), .D1(D5), .D2(D6), .D3(D7));
  Decoder_2_4 decoder_2_4_3 (.S0(S0), .S1(S1), .E(and_3_out), .D0(D8), .D1(D9), .D2(D10), .D3(D11));
  Decoder_2_4 decoder_2_4_4 (.S0(S0), .S1(S1), .E(and_4_out), .D0(D12), .D1(D13), .D2(D14), .D3(D15));
endmodule

module ALU (
  input  Cin,
  input  A,
  input  B,
  input  S1,
  input  S0,
  output Sum,
  output Cout
);

  wire multiplexer_1_out, not_1_out, not_2_out;

  not not_1 (not_1_out, 1'b1);
  not not_2 (not_2_out, B);
  Multiplexer #(.select(2), .enable("false")) multiplexer_1 (
    .in0(not_1_out), .in1(B), .in2(not_2_out), .in3(1'b1), .out(multiplexer_1_out), .sel({S1, S0}));
  FullAdder fulladder_1 (.Carry_In(Cin), .A(A), .B(multiplexer_1_out), .Sum(Sum), .Carry_Out(Cout));
endmodule

module LogicCir (
  input  A,
  input  B,
  input  S1,
  input  S0,
  output D
);

  wire and_1_out, not_1_out, or_1_out, xor_1_out;

  and and_1 (and_1_out, A, B);
  or or_1 (or_1_out, A, B);
  xor xor_1 (xor_1_out, A, B);
  not not_1 (not_1_out, A);
  Multiplexer #(.select(2), .enable("false")) multiplexer_1 (
    .in0(and_1_out), .in1(or_1_out), .in2(xor_1_out), .in3(not_1_out), .out(D), .sel({S1, S0}));
endmodule

module Alu1bit (
  input  Cin,
  input  A,
  input  B,
  input  S1,
  input  S0,
  input  Ar,
  input  Al,
  input  S2,
  input  S3,
  output OP,
  output Cout
);

  wire alu_1_sum, logiccir_1_d;

  ALU alu_1 (.A(A), .B(B), .Cin(Cin), .S1(S1), .S0(S0), .Cout(Cout), .Sum(alu_1_sum));
  LogicCir logiccir_1 (.A(A), .B(B), .S1(S1), .S0(S0), .D(logiccir_1_d));
  Multiplexer #(.select(2), .enable("false")) multiplexer_1 (
    .in0(alu_1_sum), .in1(logiccir_1_d), .in2(Ar), .in3(Al), .out(OP), .sel({S3, S2}));
endmodule

module Alu4Bit (
  input  Cin,
  input  S0,
  input  S1,
  input  S2,
  input  S3,
  input  [3:0] A,
  input  SHFTin,
  input  [3:0] B,
  output [3:0] OP,
  output Overflow,
  output SHFTout
);

  wire alu1bit_1_cout, alu1bit_2_cout, alu1bit_3_cout, D0, D1, D2, D3;

  Alu1bit alu1bit_1 (
    .A(A[0]), .B(B[0]), .S1(S1), .S0(S0), .Ar(D3), .Al(1'b0), .S2(S2), .S3(S3), .OP(OP[0]), .Cin(Cin),
    .Cout(alu1bit_1_cout));
  Alu1bit alu1bit_2 (
    .A(A[1]), .B(B[1]), .S1(S1), .S0(S0), .Ar(D2), .Al(1'b0), .S2(S2), .S3(S3), .OP(OP[1]),
    .Cin(alu1bit_1_cout), .Cout(alu1bit_2_cout));
  Alu1bit alu1bit_3 (
    .A(A[2]), .B(B[2]), .S1(S1), .S0(S0), .Ar(D1), .Al(1'b0), .S2(S2), .S3(S3), .OP(OP[2]),
    .Cin(alu1bit_2_cout), .Cout(alu1bit_3_cout));
  Alu1bit alu1bit_4 (
    .A(A[3]), .B(B[3]), .S1(S1), .S0(S0), .Ar(D0), .Al(1'b0), .S2(S2), .S3(S3), .OP(OP[3]),
    .Cin(alu1bit_3_cout), .Cout(Overflow));
  ShiftUnit shiftunit_1 (.IP(A), .Cin(Cin), .S0(S0), .S1(S1), .OP({D3, D2, D1, D0}), .BitOut(SHFTout), .BitIn(SHFTin));
endmodule

module ShiftUnit (
  input  [3:0] IP,
  input  BitIn,
  input  Cin,
  input  S0,
  input  S1,
  output [3:0] OP,
  output BitOut
);

  Multiplexer #(.select(2), .enable("false")) multiplexer_1 (
    .in0(IP[0]), .in1(IP[3]), .in2(IP[0]), .in3(IP[3]), .out(BitOut), .sel({S0, Cin}));
  Multiplexer #(.select(3), .enable("false")) multiplexer_2 (
    .in0(IP[1]), .in1(BitIn), .in2(IP[1]), .in3(1'b0), .in4(IP[1]), .in5(IP[3]), .out(OP[0]),
    .sel({S1, S0, Cin}));  // open: in6, in7
  Multiplexer #(.select(3), .enable("false")) multiplexer_3 (
    .in0(IP[2]), .in1(IP[0]), .in2(IP[2]), .in3(IP[0]), .in4(IP[2]), .in5(IP[0]), .out(OP[1]),
    .sel({S1, S0, Cin}));  // open: in6, in7
  Multiplexer #(.select(3), .enable("false")) multiplexer_4 (
    .in0(IP[3]), .in1(IP[1]), .in2(IP[3]), .in3(IP[1]), .in4(IP[3]), .in5(IP[1]), .out(OP[2]),
    .sel({S1, S0, Cin}));  // open: in6, in7
  Multiplexer #(.select(3), .enable("false")) multiplexer_5 (
    .in0(BitIn), .in1(IP[2]), .in2(IP[3]), .in3(IP[2]), .in4(IP[0]), .in5(IP[2]), .out(OP[3]),
    .sel({S1, S0, Cin}));  // open: in6, in7
endmodule
